// Logisim project project.circ as structural Verilog: 5 circuits, main circuit main
module main (
);

  wire button_1_out, button_2_out, or_1_out;
  wire [31:0] counter_1_q, t_block_1_out, t_block_2_out, t_block_3_out, t_block_4_out, t_block_5_out,
       t_block_6_out, t_block_7_out, t_block_8_out, t_block_9_out, t_block_10_out, t_block_11_out,
       t_block_12_out, t_block_13_out, t_block_14_out, t_block_15_out, t_block_16_out, undriven, undriven_2,
       undriven_3, undriven_4, undriven_5, undriven_6, undriven_7, undriven_8, undriven_9, undriven_10,
       undriven_11, undriven_12, undriven_13, undriven_14, undriven_15, undriven_16;

  T_Block t_block_1 (.A(t_block_2_out[1]), .B(1'b0), .C(t_block_1_out[1]), .OUT(t_block_1_out[0]));
  T_Block t_block_2 (.A(t_block_3_out[1]), .B(t_block_1_out[1]), .C(t_block_2_out[1]), .OUT(t_block_2_out[0]));
  T_Block t_block_3 (.A(t_block_4_out[1]), .B(t_block_2_out[1]), .C(t_block_3_out[1]), .OUT(t_block_3_out[0]));
  T_Block t_block_4 (.A(t_block_5_out[1]), .B(t_block_3_out[1]), .C(t_block_4_out[1]), .OUT(t_block_4_out[0]));
  DotMatrix #(.matrixcols(32), .matrixrows(32)) dotmatrix_1 (
    .col0(undriven), .col1(undriven_2), .col2(undriven_3), .col3(undriven_4), .col4(undriven_5),
    .col5(undriven_6), .col6(undriven_7), .col7(undriven_8), .col8(t_block_1_out), .col9(t_block_2_out),
    .col10(t_block_3_out), .col11(t_block_4_out), .col12(t_block_5_out), .col13(t_block_6_out),
    .col14(t_block_7_out), .col15(t_block_8_out), .col16(t_block_9_out), .col17(t_block_10_out),
    .col18(t_block_11_out), .col19(t_block_12_out), .col20(t_block_13_out), .col21(t_block_14_out),
    .col22(t_block_15_out), .col23(t_block_16_out), .col24(undriven_16), .col25(undriven_9),
    .col26(undriven_15), .col27(undriven_10), .col28(undriven_11), .col29(undriven_12), .col30(undriven_13),
    .col31(undriven_14));
  T_Block t_block_5 (.A(t_block_6_out[1]), .B(t_block_4_out[1]), .C(t_block_5_out[1]), .OUT(t_block_5_out[0]));
  T_Block t_block_6 (.A(t_block_7_out[1]), .B(t_block_5_out[1]), .C(t_block_6_out[1]), .OUT(t_block_6_out[0]));
  T_Block t_block_7 (.A(t_block_8_out[1]), .B(t_block_6_out[1]), .C(t_block_7_out[1]), .OUT(t_block_7_out[0]));
  T_Block t_block_8 (.A(t_block_9_out[1]), .B(t_block_7_out[1]), .C(t_block_8_out[1]), .OUT(t_block_8_out[0]));
  T_Block t_block_9 (.A(t_block_10_out[1]), .B(t_block_8_out[1]), .C(t_block_9_out[1]), .OUT(t_block_9_out[0]));
  T_Block t_block_10 (.A(t_block_11_out[1]), .B(t_block_9_out[1]), .C(t_block_10_out[1]), .OUT(t_block_10_out[0]));
  T_Block t_block_11 (.A(t_block_12_out[1]), .B(t_block_10_out[1]), .C(t_block_11_out[1]), .OUT(t_block_11_out[0]));
  T_Block t_block_12 (.A(t_block_13_out[1]), .B(t_block_11_out[1]), .C(t_block_12_out[1]), .OUT(t_block_12_out[0]));
  T_Block t_block_13 (.A(t_block_14_out[1]), .B(t_block_12_out[1]), .C(t_block_13_out[1]), .OUT(t_block_13_out[0]));
  T_Block t_block_14 (.A(t_block_15_out[1]), .B(t_block_13_out[1]), .C(t_block_14_out[1]), .OUT(t_block_14_out[0]));
  T_Block t_block_15 (.A(t_block_16_out[1]), .B(t_block_14_out[1]), .C(t_block_15_out[1]), .OUT(t_block_15_out[0]));
  T_Block t_block_16 (.A(undriven_16[0]), .B(t_block_15_out[1]), .C(t_block_16_out[1]), .OUT(t_block_16_out[0]));
  Button button_1 (.out(button_1_out));
  Button button_2 (.out(button_2_out));
  or or_1 (or_1_out, button_1_out, button_2_out);
  // Probe on counter_1_q
  Counter #(.width(32), .max('h1f)) counter_1 (
    .load(button_1_out), .Q(counter_1_q), .clk(or_1_out));  // open: D, count, carry, clr
  \трансформатор  \u_трансформатор_1  (
    .in_1(counter_1_q[4:0]),
    .out_2({undriven[0], undriven_2[0], undriven_3[0], undriven_4[0], undriven_5[0], undriven_6[0], undriven_7[0], undriven_8[0], t_block_1_out[1], t_block_2_out[1], t_block_3_out[1], t_block_4_out[1], t_block_5_out[1], t_block_6_out[1], t_block_7_out[1], t_block_8_out[1], t_block_9_out[1], t_block_10_out[1], t_block_11_out[1], t_block_12_out[1], t_block_13_out[1], t_block_14_out[1], t_block_15_out[1], t_block_16_out[1], undriven_16[0], undriven_9[0], undriven_15[0], undriven_10[0], undriven_11[0], undriven_12[0], undriven_13[0], undriven_14[0]}));
endmodule

module \трансформатор  (
  input  [4:0] in_1,
  output [31:0] out_2
);

  Comparator #(.width(5), .mode("unsigned")) comparator_1 (.a(in_1), .b({5{1'b0}}), .eq(out_2[0]));  // open: gt, lt
  Comparator #(.width(5), .mode("unsigned")) comparator_2 (.a(in_1), .b(5'b00001), .eq(out_2[1]));  // open: gt, lt
  Comparator #(.width(5), .mode("unsigned")) comparator_3 (.a(in_1), .b(5'b00010), .eq(out_2[2]));  // open: gt, lt
  Comparator #(.width(5), .mode("unsigned")) comparator_4 (.a(in_1), .b(5'b00011), .eq(out_2[3]));  // open: gt, lt
  Comparator #(.width(5), .mode("unsigned")) comparator_5 (.a(in_1), .b(5'b00100), .eq(out_2[4]));  // open: gt, lt
  Comparator #(.width(5), .mode("unsigned")) comparator_6 (.a(in_1), .b(5'b00101), .eq(out_2[5]));  // open: gt, lt
  Comparator #(.width(5), .mode("unsigned")) comparator_7 (.a(in_1), .b(5'b00110), .eq(out_2[6]));  // open: gt, lt
  Comparator #(.width(5), .mode("unsigned")) comparator_8 (.a(in_1), .b(5'b00111), .eq(out_2[7]));  // open: gt, lt
  Comparator #(.width(5), .mode("unsigned")) comparator_9 (.a(in_1), .b(5'b01000), .eq(out_2[8]));  // open: gt, lt
  Comparator #(.width(5), .mode("unsigned")) comparator_10 (.a(in_1), .b(5'b01001), .eq(out_2[9]));  // open: gt, lt
  Comparator #(.width(5), .mode("unsigned")) comparator_11 (.a(in_1), .b(5'b01010), .eq(out_2[10]));  // open: gt, lt
  Comparator #(.width(5), .mode("unsigned")) comparator_12 (.a(in_1), .b(5'b01011), .eq(out_2[11]));  // open: gt, lt
  Comparator #(.width(5), .mode("unsigned")) comparator_13 (.a(in_1), .b(5'b01100), .eq(out_2[12]));  // open: gt, lt
  Comparator #(.width(5), .mode("unsigned")) comparator_14 (.a(in_1), .b(5'b01101), .eq(out_2[13]));  // open: gt, lt
  Comparator #(.width(5), .mode("unsigned")) comparator_15 (.a(in_1), .b(5'b01110), .eq(out_2[14]));  // open: gt, lt
  Comparator #(.width(5), .mode("unsigned")) comparator_16 (.a(in_1), .b(5'b01111), .eq(out_2[15]));  // open: gt, lt
  Comparator #(.width(5), .mode("unsigned")) comparator_17 (.a(in_1), .b(5'b10000), .eq(out_2[16]));  // open: gt, lt
  Comparator #(.width(5), .mode("unsigned")) comparator_18 (.a(in_1), .b(5'b10001), .eq(out_2[17]));  // open: gt, lt
  Comparator #(.width(5), .mode("unsigned")) comparator_19 (.a(in_1), .b(5'b10010), .eq(out_2[18]));  // open: gt, lt
  Comparator #(.width(5), .mode("unsigned")) comparator_20 (.a(in_1), .b(5'b10011), .eq(out_2[19]));  // open: gt, lt
  Comparator #(.width(5), .mode("unsigned")) comparator_21 (.a(in_1), .b(5'b10100), .eq(out_2[20]));  // open: gt, lt
  Comparator #(.width(5), .mode("unsigned")) comparator_22 (.a(in_1), .b(5'b10101), .eq(out_2[21]));  // open: gt, lt
  Comparator #(.width(5), .mode("unsigned")) comparator_23 (.a(in_1), .b(5'b10110), .eq(out_2[22]));  // open: gt, lt
  Comparator #(.width(5), .mode("unsigned")) comparator_24 (.a(in_1), .b(5'b10111), .eq(out_2[23]));  // open: gt, lt
  Comparator #(.width(5), .mode("unsigned")) comparator_25 (.a(in_1), .b(5'b11000), .eq(out_2[24]));  // open: gt, lt
  Comparator #(.width(5), .mode("unsigned")) comparator_26 (.a(in_1), .b(5'b11001), .eq(out_2[25]));  // open: gt, lt
  Comparator #(.width(5), .mode("unsigned")) comparator_27 (.a(in_1), .b(5'b11010), .eq(out_2[26]));  // open: gt, lt
  Comparator #(.width(5), .mode("unsigned")) comparator_28 (.a(in_1), .b(5'b11011), .eq(out_2[27]));  // open: gt, lt
  Comparator #(.width(5), .mode("unsigned")) comparator_29 (.a(in_1), .b(5'b11100), .eq(out_2[28]));  // open: gt, lt
  Comparator #(.width(5), .mode("unsigned")) comparator_30 (.a(in_1), .b(5'b11101), .eq(out_2[29]));  // open: gt, lt
  Comparator #(.width(5), .mode("unsigned")) comparator_31 (.a(in_1), .b(5'b11110), .eq(out_2[30]));  // open: gt, lt
  Comparator #(.width(5), .mode("unsigned")) comparator_32 (.a(in_1), .b({5{1'b1}}), .eq(out_2[31]));  // open: gt, lt
endmodule

module \инкремент  (
  input  [4:0] X,
  output [4:0] R,
  output Cout
);

  wire [4:1] and_1_out;

  assign {Cout, and_1_out} = {and_1_out, 1'b1} & X;  // AND_Gate and_1, 5 bits wide
  assign R = X ^ {and_1_out, 1'b1};  // XOR_Gate xor_1, 5 bits wide
endmodule

module \декремент  (
  input  [7:0] X,
  output [7:0] R,
  output Cout
);

  wire [7:1] and_1_out;
  wire [7:7] and_1_out_2;

  assign R = ~(X ^ ~{and_1_out, 1'b1});  // XNOR_Gate xnor_1, 8 bits wide
  assign {and_1_out_2[7], and_1_out} = ~X & {and_1_out, 1'b1};  // AND_Gate and_1, 8 bits wide
  Multiplexer #(.disabled(0), .enable("false")) multiplexer_1 (
    .in0(1'b1), .in1(1'b0), .out(Cout), .sel(and_1_out_2[7]));
endmodule

module T_Block (
  input  A,
  input  B,
  input  C,
  output OUT
);

  or or_1 (OUT, A, B, C);
endmodule
